# Fritzing sketch trixie-digital-gauge (saved by Fritzing 0.9.3b)

parts:
  Part1 = Adafruit Perma-Proto HAT [part_number="Adafruit #2314 and #2310"]
  Part2 = OLED Color 1.5 inch 128x128 w microSD [part_number=1431]
  ADC1 = MCP3008 [package=dil16]

nets:
  N1: Part1.SPI_MOSI, Part1.N$52, Part2.MOSI, ADC1.Din
  N2: Part1.SPI_MISO, Part1.N$54, Part2.SD_MISO, ADC1.Dout
  N3: Part1.SPI_SCLK, Part1.N$53, Part2.SCK, ADC1.CLK
  3.3V: Part1.3.3V, Part1.N$56, Part1.N$57, Part2.3.3V, ADC1.VREF, ADC1.VDD
  GND: Part1.GND, Part1.N$49, Part1.N$55, Part2.GND, ADC1.DGND, ADC1.AGND
  N4: Part1.N$6, ADC1.CH0
  N5: Part1.N$7, ADC1.CH2
  N6: Part1.N$8, ADC1.CH1
  N7: Part1.N$9, ADC1.CH3
  N8: Part1.N$10, ADC1.CH4
  N9: Part1.N$11, ADC1.CH5
  N10: Part1.N$12, ADC1.CH6
  N11: Part1.N$13, ADC1.CH7
  N12: Part1.N$51, ADC1.CS/SHDN

custom parts:
  Adafruit Perma-Proto HAT: To kick off the Adafruit HAT party, we have this Perma-Proto inspired plug in daughter board. It has a grid of 0.1" prototyping soldering holes for attaching chips, resistors, LED, potentiometers and more. The holes are connected underneath with traces to mimic the solderless breadboards you're familiar. There's also long power strips for +3V, +5V and Ground connections to the Pi. Near the top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
  OLED Color 1.5 inch 128x128 w microSD: The visible portion of this OLED measures 1.5" diagonal and contains 128x128 RGB pixels, each one made of red, green and blue OLEDs. Each pixel can be set with 16-bits of resolution for a large range of colors. Because the display uses OLEDs, there is no backlight, and the contrast is very high (black is really black). We picked this display for its excellent color, this is the nicest mini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
